// Digital circuit inst-decoder.dig as structural Verilog
module inst_decoder (
  input  [31:0] IW,
  output WDsel,
  output PCsel,
  output [1:0] ALUSrcB,
  output ALUSrcA,
  output [2:0] ALUOp,
  output RFW
);

  wire ADDI_eq, ADDR_eq, jal_eq_1_eq, jalr_eq_1_eq;
  wire [1:0] priorityencoder_1_num;

  opcode_funct3_eq ADDI (
    .opcode(IW[6:0]), .funct3(IW[14:12]), .iw_funct3(3'b000), .iw_opcode(7'b0010011), .eq(ADDI_eq));
  opcode_funct3_funct7_eq ADDR (
    .iw_opcode(IW[6:0]), .iw_funct3(IW[14:12]), .iw_funct7(IW[31:25]), .funct7({7{1'b0}}),
    .opcode(7'b0110011), .funct3(3'b000), .eq(ADDR_eq));
  jal_eq jal_eq_1 (.opcode(IW[6:0]), .eq(jal_eq_1_eq));
  jalr_eq jalr_eq_1 (.opcode(IW[6:0]), .funct3(IW[14:12]), .eq(jalr_eq_1_eq));
  PriorityEncoder #(.Selector_Bits(2)) priorityencoder_1 (
    .in0(ADDI_eq), .in1(ADDR_eq), .in2(jal_eq_1_eq), .in3(jalr_eq_1_eq), .num(priorityencoder_1_num));  // open: any
  ROM #(.Bits(9)) rom_1 (.A(priorityencoder_1_num), .sel(1'b1), .D({RFW, ALUOp, ALUSrcA, ALUSrcB, PCsel, WDsel}));

  // Notes on the sheet:
  //   contents of rom_1 (hex, n*v repeats v):
  //   104,100,11b,107
endmodule
